# Fritzing sketch pcb-ok-ultrasonic+wi-fi (saved by Fritzing 0.9.3b)
circuit board: 6.2cm x 6.5cm
breadboards: 1

parts:
  arduino_nano = Arduino Nano (Rev3.0) (ICSP)
  ir_senzor = screw terminal, 3 pins
  nema11 = screw terminal, 4 pins
  C2 = Electrolytic Capacitor [capacitance=100µF package="100 mil [THT, electrolytic]"]
  Tera = screw terminal, 5 pins
  C1 = Electrolytic Capacitor [capacitance=1µF package="100 mil [THT, electrolytic]"]
  Q1 = PNP-Transistor [package="TO92 [THT]"]
  C5 = Ceramic Capacitor [capacitance=100nF package="100 mil [THT, multilayer]"]
  C3 = Ceramic Capacitor [capacitance=100nF package="100 mil [THT, multilayer]"]
  12V = Screw terminal - 2 pins [package=THT]
  A4988 = Pololu A4988 [package=SO16]
  Wi-Fi = shrouded pin header, 8 pins [form="♂ (shrouded male)"]
  ultrasonic = screw terminal, 4 pins

nets (from the pcb view):
  N1: arduino_nano.D1/TX, Wi-Fi.pin1
  N2: arduino_nano.D0/RX, Wi-Fi.pin5
  GND: arduino_nano.GND, ir_senzor.pin1, C2.-, Tera.pin1, Tera.pin3, C1.-, Q1.B, C5.1, C3.0, 12V.pin1, A4988.GND, Wi-Fi.pin2, Wi-Fi.pin4, ultrasonic.pin1
  N3: arduino_nano.D2, A4988.DIR
  N4: arduino_nano.D3, A4988.STEP
  N5: arduino_nano.D4, A4988.ENABLE
  N6: arduino_nano.D5, ir_senzor.pin2
  N7: arduino_nano.D7, ultrasonic.pin2
  N8: arduino_nano.D8, ultrasonic.pin3
  N9: arduino_nano.VIN, Tera.pin2, Q1.E, C5.0
  5V: arduino_nano.5V, ir_senzor.pin3, C1.+, A4988.MS1, A4988.MS2, A4988.MS3, A4988.VDD, ultrasonic.pin4
  N10: arduino_nano.A5, Tera.pin4
  N11: arduino_nano.A4, Tera.pin5
  N12: arduino_nano.3V3, Wi-Fi.pin6, Wi-Fi.pin8
  N13: nema11.pin1, A4988.2B
  N14: nema11.pin2, A4988.2A
  N15: nema11.pin3, A4988.1A
  N16: nema11.pin4, A4988.1B
  N17: C2.+, Q1.C, C3.1, 12V.pin2, A4988.VMOT
  N18: A4988.RESET, A4988.SLEEP
